// Digital circuit ALU8Bits.dig as structural Verilog
module ALU8Bits (
  input  [7:0] A,
  input  [7:0] B,
  input  Cin,
  input  [3:0] OP,
  output [7:0] Y,
  output [7:0] ST
);

  wire add_1_c_o, lsl8_1_p4, lsr8_1_p4, sub_1_c_o, sub_2_c_o, sub_3_c_o;
  wire [7:0] add_1_s, and_1_out, lsl8_1_p3, lsr8_1_p3, not_1_out, or_1_out, sub_1_s, sub_2_s, sub_3_s,
       xor_1_out;

  Comparator #(.Signed("true"), .Bits(8)) comparator_1 (.a(A), .b({8{1'b0}}), .eq(ST[0]));  // open: gt, lt
  Comparator #(.Signed("true"), .Bits(8)) comparator_2 (.a(A), .b(B), .gt(ST[2]), .eq(ST[1]), .lt(ST[3]));
  assign not_1_out = ~A;  // Not not_1, 8 bits wide
  assign or_1_out = A | B;  // Or or_1, 8 bits wide
  assign and_1_out = A & B;  // And and_1, 8 bits wide
  assign xor_1_out = A ^ B;  // XOr xor_1, 8 bits wide
  Add #(.Bits(8)) add_1 (.a(A), .b(B), .c_i(Cin), .s(add_1_s), .c_o(add_1_c_o));
  Sub #(.Bits(8)) sub_1 (.a(A), .b(B), .c_i(Cin), .s(sub_1_s), .c_o(sub_1_c_o));
  Sub #(.Bits(8)) sub_2 (.a(A), .b(8'h1), .c_i(1'b0), .s(sub_2_s), .c_o(sub_2_c_o));
  Sub #(.Bits(8)) sub_3 (.a(B), .b(8'h1), .c_i(1'b0), .s(sub_3_s), .c_o(sub_3_c_o));
  // LSL8 lsl8_1: pin names not known; wires that end beside it: A, Cin, lsl8_1_p3, lsl8_1_p4
  // LSR8 lsr8_1: pin names not known; wires that end beside it: A, Cin, lsr8_1_p3, lsr8_1_p4
  Multiplexer #(.Selector_Bits(4), .Bits(8)) multiplexer_1 (
    .sel(OP), .in_0(A), .in_1(B), .in_2(not_1_out), .in_3(or_1_out), .in_4(and_1_out), .in_5(xor_1_out),
    .in_6(add_1_s), .in_7(sub_1_s), .in_8(sub_2_s), .in_9(sub_3_s), .in_10(lsl8_1_p3), .in_11(lsr8_1_p3),
    .in_12({8{1'b0}}), .in_13({8{1'b0}}), .in_14({8{1'b0}}), .in_15({8{1'b0}}), .out(Y));
  Multiplexer #(.Selector_Bits(4)) multiplexer_2 (
    .sel(OP), .in_0(1'b0), .in_1(1'b0), .in_2(1'b0), .in_3(1'b0), .in_4(1'b0), .in_5(1'b0), .in_6(add_1_c_o),
    .in_7(sub_1_c_o), .in_8(sub_2_c_o), .in_9(sub_3_c_o), .in_10(lsl8_1_p4), .in_11(lsr8_1_p4), .in_12(1'b0),
    .in_13(1'b0), .in_14(1'b0), .in_15(1'b0), .out(ST[5]));

  assign {ST[7:6], ST[4]} = {2'b00, A[7]};

  // Other names for the same wires on the sheet: N = A[7]; C = ST[5]; E = ST[1]; G = ST[2]; S = ST[3]; Z = ST[0]
endmodule
