// Digital circuit BasicReg1.dig as structural Verilog
module BasicReg1 (
  input  E,
  input  CLK,
  input  CLR,
  input  D,
  input  S,
  input  R,
  output Q
);

  wire and_1_out, or_1_out;

  and and_1 (and_1_out, E, CLK);
  or or_1 (or_1_out, CLR, R);
  D_FF_AS d_ff_as_1 (.Set(S), .D(D), .C(and_1_out), .Clr(or_1_out), .Q(Q));  // open: nQ
endmodule
