// Digital circuit BasicReg8.dig as structural Verilog
module BasicReg8 (
  input  E,
  input  CLK,
  input  R,
  input  [7:0] D,
  output [7:0] Q
);

  wire and_1_out;

  and and_1 (and_1_out, E, CLK);
  D_FF_AS #(.Bits(8)) d_ff_as_1 (.Set(1'b0), .D(D), .C(and_1_out), .Clr(R), .Q(Q));  // open: nQ
endmodule
