// Digital circuit CPU8Bit1K.dig as structural Verilog
module CPU8Bit1K (
  input  RST,
  input  [7:0] BusIn,
  input  Clock,
  input  [7:0] PromIN,
  input  [27:0] CtrlRomData,
  input  [7:0] RamIn,
  output [7:0] BusOut,
  output [9:0] AddrBus,
  output OutE,
  output InE,
  output [9:0] PromAddr,
  output [5:0] CtrlRomAddr,
  output RamE,
  output RamOe
);

  wire and_1_out, C, Cout, E, G, multiplexer_1_out, N, S, Z;
  wire [1:0] A89;
  wire [7:0] A, alu8bits_1_y, B, multiplexer_2_out, multiplexer_4_out;
  wire [7:6] alu8bits_1_st;
  wire [9:0] AR, PC;

  Multiplexer #(.Selector_Bits(3)) multiplexer_1 (
    .sel(CtrlRomData[14:12]), .in_0(1'b0), .in_1(1'b1), .in_2(Z), .in_3(E), .in_4(G), .in_5(S), .in_6(N),
    .in_7(C), .out(multiplexer_1_out));
  // Probe PC on PC
  // Probe BUS on BusOut
  // Probe A on A
  // Probe B on B
  // Probe AR on AR
  // Probe IR on {A89, CtrlRomAddr}
  // Probe Cout on Cout
  // Probe C on C
  Multiplexer #(.Bits(8)) multiplexer_2 (.sel(CtrlRomData[26]), .in_0(alu8bits_1_y), .in_1(B), .out(multiplexer_2_out));
  Reg10ir PC_2 (.E(multiplexer_1_out), .INC(1'b1), .nCLK(Clock), .R(RST), .D({A89, PromIN}), .Q(PC));
  and and_1 (and_1_out, CtrlRomData[4], ~Clock);  // And
  // Probe BusMux0 on CtrlRomData[0]
  // Probe BusMux1 on CtrlRomData[1]
  // Probe AluBMux on CtrlRomData[2]
  // Probe IRZ on CtrlRomData[3]
  // Probe PRomAMux on CtrlRomData[4]
  // Probe RamAMux on CtrlRomData[5]
  // Probe RamOU on CtrlRomData[6]
  // Probe RamE on CtrlRomData[7]
  Reg8i A_2 (.E(CtrlRomData[17]), .INC(CtrlRomData[18]), .CLK(Clock), .R(RST), .D(multiplexer_2_out), .Q(A));
  ALU8Bits alu8bits_1 (
    .Y(alu8bits_1_y), .A(A), .B(multiplexer_4_out), .ST({alu8bits_1_st, Cout, N, S, G, E, Z}), .Cin(C),
    .OP(CtrlRomData[11:8]));
  Reg8 IR_2 (.D(PromIN), .Q({A89, CtrlRomAddr}), .SR(CtrlRomData[3]), .nCLK(Clock));
  Multiplexer #(.Bits(10)) multiplexer_3 (.sel(and_1_out), .in_0(PC), .in_1(AR), .out(PromAddr));
  // Probe OP0 on CtrlRomData[8]
  // Probe OP1 on CtrlRomData[9]
  // Probe OP2 on CtrlRomData[10]
  // Probe OP3 on CtrlRomData[11]
  // Probe PCM0 on CtrlRomData[12]
  // Probe PCM1 on CtrlRomData[13]
  // Probe PCM2 on CtrlRomData[14]
  // Probe INE on CtrlRomData[15]
  Reg8i B_2 (.E(CtrlRomData[19]), .INC(CtrlRomData[20]), .CLK(Clock), .R(RST), .D(BusOut), .Q(B));
  Multiplexer #(.Bits(8)) multiplexer_4 (.sel(CtrlRomData[2]), .in_0(BusOut), .in_1(B), .out(multiplexer_4_out));
  Multiplexer #(.Selector_Bits(2), .Bits(8)) multiplexer_5 (
    .sel(CtrlRomData[1:0]), .in_0(alu8bits_1_y), .in_1(BusIn), .in_2(PromIN), .in_3(RamIn), .out(BusOut));
  Reg10i AR_2 (.E(CtrlRomData[21]), .INC(CtrlRomData[22]), .CLK(Clock), .R(RST), .D({A89, BusOut}), .Q(AR));
  BasicReg1 C_CARRY (
    .Q(C), .S(CtrlRomData[23]), .D(Cout), .E(CtrlRomData[24]), .CLK(Clock), .CLR(CtrlRomData[25]), .R(RST));
  // Probe OUTE on CtrlRomData[16]
  // Probe AE on CtrlRomData[17]
  // Probe AINC on CtrlRomData[18]
  // Probe BE on CtrlRomData[19]
  // Probe BINC on CtrlRomData[20]
  // Probe ARE on CtrlRomData[21]
  // Probe ARINC on CtrlRomData[22]
  // Probe CSET on CtrlRomData[23]
  Multiplexer #(.Bits(10)) multiplexer_6 (.sel(CtrlRomData[5]), .in_0(AR), .in_1({A89, PromIN}), .out(AddrBus));
  // Probe CE on CtrlRomData[24]
  // Probe CCLR on CtrlRomData[25]
  // Probe AMux on CtrlRomData[26]
  // Probe Reserva on CtrlRomData[27]

  assign InE = CtrlRomData[15];
  assign OutE = CtrlRomData[16];
  assign RamE = CtrlRomData[7];
  assign RamOe = CtrlRomData[6];

  // Other names for the same wires on the sheet: BUS[7:0] = BusOut; CLK = Clock; BusMux0 = CtrlRomData[0];
  //   BusMux1 = CtrlRomData[1]; AluBMux = CtrlRomData[2]; IRZ = CtrlRomData[3]; PRomAMux = CtrlRomData[4];
  //   RamAMux = CtrlRomData[5]; OP0 = CtrlRomData[8]; OP1 = CtrlRomData[9]; OP2 = CtrlRomData[10];
  //   OP3 = CtrlRomData[11]; PCM0 = CtrlRomData[12]; PCM1 = CtrlRomData[13]; PCM2 = CtrlRomData[14];
  //   AE = CtrlRomData[17]; AINC = CtrlRomData[18]; BE = CtrlRomData[19]; BINC = CtrlRomData[20];
  //   ARE = CtrlRomData[21]; ARINC = CtrlRomData[22]; CSET = CtrlRomData[23]; CE = CtrlRomData[24];
  //   CCLR = CtrlRomData[25]; AMux = CtrlRomData[26]; Reserva = CtrlRomData[27]; IR[7:0] = {A89, CtrlRomAddr};
  //   PROM[7:0] = PromIN; RESET = RST

  // Notes on the sheet:
  //   RST: default 1
  //   Clock: Hz: 10
  //   Version 0.4
endmodule
