// Digital circuit CpuRamRom.dig as structural Verilog
module CpuRamRom (
  input  RST,
  input  [7:0] BusIn,
  input  Clock,
  input  [7:0] PromIN,
  input  [7:0] RamIn,
  output [7:0] BusOut,
  output [2:0] AddrBus,
  output OutE,
  output InE,
  output [3:0] PromAddr,
  output RamE,
  output RamOe
);

  wire [5:0] cpu8bit1k_1_ctrlromaddr;
  wire [9:3] cpu8bit1k_1_addrbus;
  wire [9:4] cpu8bit1k_1_promaddr;
  wire [27:0] Ctrl_d;

  ROM #(.AddrBits(6), .Bits(28)) Ctrl (.A(cpu8bit1k_1_ctrlromaddr), .sel(1'b1), .D(Ctrl_d));
  CPU8Bit1K cpu8bit1k_1 (
    .RST(RST), .BusIn(BusIn), .Clock(Clock), .PromIN(PromIN), .CtrlRomData(Ctrl_d), .RamIn(RamIn),
    .BusOut(BusOut), .AddrBus({cpu8bit1k_1_addrbus, AddrBus}), .OutE(OutE), .InE(InE),
    .PromAddr({cpu8bit1k_1_promaddr, PromAddr}), .CtrlRomAddr(cpu8bit1k_1_ctrlromaddr), .RamE(RamE),
    .RamOe(RamOe));

  // Notes on the sheet:
  //   RST: default 1
  //   Clock: Hz: 10
  //   contents of Ctrl (hex, n*v repeats v):
  //   0,2010a,8000a,20000a,20112,80012,420112,480012,80000,20104,80
  //   ,184,400080,400184,a8,1ac,20143,80043,420143,480043,2016b,8006b
  //   ,28101,88001,428101,488001,28129,88029,10000,10104,1000a,410000
  //   ,410104,41000a,10028,1012c,40000,100000,400000,1008,2008,300c
  //   ,400c,500c,6008,7008,1800000,3000000,20200,20304,2030a,20404,2040a
  //   ,20504,2050a,1020604,102060a,1020704,102070a,1020800,1080904,1020a00
  //   ,1020b00,40a0000
endmodule
