// Digital circuit DIV50M100HZ.dig as structural Verilog
module DIV50M100HZ (
  input  Clock50M,
  output y
);

  wire comparator_1_eq, d_ff_1_nq;
  wire [24:0] counter_1_out;

  Counter #(.Bits(25)) counter_1 (.en(1'b1), .C(Clock50M), .clr(comparator_1_eq), .out(counter_1_out));  // open: ovf
  Comparator #(.Bits(25)) comparator_1 (.a(counter_1_out), .b(25'h3d090), .eq(comparator_1_eq));  // open: gt, lt
  D_FF d_ff_1 (.D(d_ff_1_nq), .C(comparator_1_eq), .Q(y), .nQ(d_ff_1_nq));
endmodule
