// Digital circuit Decoder4e.dig as structural Verilog
module Decoder4e (
  input  [1:0] in,
  input  E,
  output _0,
  output _1,
  output _2,
  output _3
);

  wire decoder_1_out_0, decoder_1_out_1, decoder_1_out_2, decoder_1_out_3;

  Decoder #(.Selector_Bits(2)) decoder_1 (
    .sel(in), .out_0(decoder_1_out_0), .out_1(decoder_1_out_1), .out_2(decoder_1_out_2),
    .out_3(decoder_1_out_3));
  and and_1 (_0, decoder_1_out_0, E);
  and and_2 (_1, decoder_1_out_1, E);
  and and_3 (_2, decoder_1_out_2, E);
  and and_4 (_3, decoder_1_out_3, E);
endmodule
