// Digital circuit Demux8.dig as structural Verilog
module Demux8 (
  input  [7:0] I,
  input  S,
  output [7:0] O0,
  output [7:0] O1
);

  wire not_1_out;

  not not_1 (not_1_out, S);
  assign O0 = not_1_out ? I : 8'bz;  // Driver driver_1
  assign O1 = S ? I : 8'bz;  // Driver driver_2
endmodule
