// Digital circuit Driver7Seg.dig as structural Verilog
module Driver7Seg (
  input  D0,
  input  D1,
  input  D2,
  input  D3,
  input  Inv,
  output a,
  output b,
  output c,
  output d,
  output e,
  output f,
  output g
);

  wire [6:0] dec7seg_out;

  LookUpTable #(.Bits(7)) dec7seg (.in0(D0), .in1(D1), .in2(D2), .in3(D3), .out(dec7seg_out));
  xor xor_1 (a, dec7seg_out[0], Inv);
  xor xor_2 (b, dec7seg_out[1], Inv);
  xor xor_3 (c, dec7seg_out[2], Inv);
  xor xor_4 (d, dec7seg_out[3], Inv);
  xor xor_5 (e, dec7seg_out[4], Inv);
  xor xor_6 (f, dec7seg_out[5], Inv);
  xor xor_7 (g, dec7seg_out[6], Inv);

  // Notes on the sheet:
  //   contents of dec7seg (hex, n*v repeats v):
  //   3f,6,5b,4f,66,6d,7d,7,7f,6f,77,7c,39,5e,79,71
endmodule
