// Digital circuit Reg10ir.dig as structural Verilog
module Reg10ir (
  input  E,
  input  [9:0] D,
  input  nCLK,
  input  R,
  input  INC,
  output [9:0] Q
);

  wire and_1_out, and_2_out, and_3_out, and_4_out, and_5_out, and_6_out, and_7_out, and_8_out, and_9_out,
       d_ff_as_1_nq, multiplexer_1_out, multiplexer_2_out, multiplexer_3_out, multiplexer_4_out,
       multiplexer_5_out, multiplexer_6_out, multiplexer_7_out, multiplexer_8_out, multiplexer_9_out,
       multiplexer_10_out, not_1_out, or_1_out, xor_1_out, xor_2_out, xor_3_out, xor_4_out, xor_5_out,
       xor_6_out, xor_7_out, xor_8_out, xor_9_out;

  not not_1 (not_1_out, nCLK);
  or or_1 (or_1_out, E, INC);
  and and_1 (and_1_out, or_1_out, not_1_out);
  Multiplexer multiplexer_1 (.sel(E), .in_0(d_ff_as_1_nq), .in_1(D[0]), .out(multiplexer_1_out));
  D_FF_AS d_ff_as_1 (.Set(1'b0), .D(multiplexer_1_out), .C(and_1_out), .Clr(R), .Q(Q[0]), .nQ(d_ff_as_1_nq));
  xor xor_1 (xor_1_out, Q[1], Q[0]);
  Multiplexer multiplexer_2 (.sel(E), .in_0(xor_1_out), .in_1(D[1]), .out(multiplexer_2_out));
  D_FF_AS d_ff_as_2 (.Set(1'b0), .D(multiplexer_2_out), .C(and_1_out), .Clr(R), .Q(Q[1]));  // open: nQ
  and and_2 (and_2_out, Q[0], Q[1]);
  xor xor_2 (xor_2_out, Q[2], and_2_out);
  Multiplexer multiplexer_3 (.sel(E), .in_0(xor_2_out), .in_1(D[2]), .out(multiplexer_3_out));
  D_FF_AS d_ff_as_3 (.Set(1'b0), .D(multiplexer_3_out), .C(and_1_out), .Clr(R), .Q(Q[2]));  // open: nQ
  and and_3 (and_3_out, and_2_out, Q[2]);
  xor xor_3 (xor_3_out, Q[3], and_3_out);
  Multiplexer multiplexer_4 (.sel(E), .in_0(xor_3_out), .in_1(D[3]), .out(multiplexer_4_out));
  D_FF_AS d_ff_as_4 (.Set(1'b0), .D(multiplexer_4_out), .C(and_1_out), .Clr(R), .Q(Q[3]));  // open: nQ
  and and_4 (and_4_out, and_3_out, Q[3]);
  xor xor_4 (xor_4_out, Q[4], and_4_out);
  Multiplexer multiplexer_5 (.sel(E), .in_0(xor_4_out), .in_1(D[4]), .out(multiplexer_5_out));
  D_FF_AS d_ff_as_5 (.Set(1'b0), .D(multiplexer_5_out), .C(and_1_out), .Clr(R), .Q(Q[4]));  // open: nQ
  and and_5 (and_5_out, and_4_out, Q[4]);
  xor xor_5 (xor_5_out, Q[5], and_5_out);
  Multiplexer multiplexer_6 (.sel(E), .in_0(xor_5_out), .in_1(D[5]), .out(multiplexer_6_out));
  D_FF_AS d_ff_as_6 (.Set(1'b0), .D(multiplexer_6_out), .C(and_1_out), .Clr(R), .Q(Q[5]));  // open: nQ
  and and_6 (and_6_out, and_5_out, Q[5]);
  xor xor_6 (xor_6_out, Q[6], and_6_out);
  Multiplexer multiplexer_7 (.sel(E), .in_0(xor_6_out), .in_1(D[6]), .out(multiplexer_7_out));
  D_FF_AS d_ff_as_7 (.Set(1'b0), .D(multiplexer_7_out), .C(and_1_out), .Clr(R), .Q(Q[6]));  // open: nQ
  and and_7 (and_7_out, and_6_out, Q[6]);
  xor xor_7 (xor_7_out, Q[7], and_7_out);
  Multiplexer multiplexer_8 (.sel(E), .in_0(xor_7_out), .in_1(D[7]), .out(multiplexer_8_out));
  D_FF_AS d_ff_as_8 (.Set(1'b0), .D(multiplexer_8_out), .C(and_1_out), .Clr(R), .Q(Q[7]));  // open: nQ
  and and_8 (and_8_out, and_7_out, Q[7]);
  xor xor_8 (xor_8_out, Q[8], and_8_out);
  Multiplexer multiplexer_9 (.sel(E), .in_0(xor_8_out), .in_1(D[8]), .out(multiplexer_9_out));
  D_FF_AS d_ff_as_9 (.Set(1'b0), .D(multiplexer_9_out), .C(and_1_out), .Clr(R), .Q(Q[8]));  // open: nQ
  and and_9 (and_9_out, and_8_out, Q[8]);
  xor xor_9 (xor_9_out, Q[9], and_9_out);
  Multiplexer multiplexer_10 (.sel(E), .in_0(xor_9_out), .in_1(D[9]), .out(multiplexer_10_out));
  D_FF_AS d_ff_as_10 (.Set(1'b0), .D(multiplexer_10_out), .C(and_1_out), .Clr(R), .Q(Q[9]));  // open: nQ
endmodule
