// Digital circuit Reg8.dig as structural Verilog
module Reg8 (
  input  [7:0] D,
  input  R,
  input  nCLK,
  input  SR,
  output [7:0] Q
);

  wire [7:0] multiplexer_1_out;

  Multiplexer #(.Bits(8)) multiplexer_1 (.sel(SR), .in_0(D), .in_1({8{1'b0}}), .out(multiplexer_1_out));
  D_FF_AS #(.Bits(8)) d_ff_as_1 (.Set(1'b0), .D(multiplexer_1_out), .C(~nCLK), .Clr(R), .Q(Q));  // open: nQ
endmodule
