// Digital circuit TesteCpuDidatica.dig as structural Verilog
module TesteCpuDidatica (
  input  Clock,
  input  [3:0] inp,
  output a,
  output b,
  output c,
  output d,
  output e,
  output f,
  output g,
  output dig0,
  output dig1,
  output L0,
  output L1,
  output L2,
  output L3,
  output dig2,
  output dig3,
  output dp
);

  wire cpu8bit1k_1_oute, decoder4e_1__0, decoder4e_1__1, decoder4e_1__2, decoder_1_out_0, decoder_1_out_1,
       decoder_1_out_2, decoder_1_out_3, div50m1khz_1_y;
  wire [1:0] counter_1_out;
  wire [3:0] multiplexer_1_out;
  wire [7:0] cpu8bit1k_1_out, PROM_d, saida0_q, saida1_q, saida2_q;
  wire [7:4] not_1_out;
  wire [9:0] cpu8bit1k_1_addrbus, cpu8bit1k_1_promaddr;

  DIV50M1KHZ div50m1khz_1 (.Clock50M(Clock), .y(div50m1khz_1_y));
  ROM #(.AddrBits(10), .Bits(8)) PROM (.A(cpu8bit1k_1_promaddr), .sel(1'b1), .D(PROM_d));
  CPU8Bit1K cpu8bit1k_1 (
    .RST(1'b0), .IN({4'b0000, inp}), .Clock(div50m1khz_1_y), .PromIN(PROM_d), .OUT(cpu8bit1k_1_out),
    .AddrBus(cpu8bit1k_1_addrbus), .OutE(cpu8bit1k_1_oute), .PromAddr(cpu8bit1k_1_promaddr));  // open: InE
  // Probe on cpu8bit1k_1_addrbus
  Decoder4e decoder4e_1 (
    .in(cpu8bit1k_1_addrbus[1:0]), .E(cpu8bit1k_1_oute), ._0(decoder4e_1__0), ._1(decoder4e_1__1),
    ._2(decoder4e_1__2));  // open: _3
  BasicReg8 saida2 (.Q(saida2_q), .D(cpu8bit1k_1_out), .E(decoder4e_1__2), .CLK(div50m1khz_1_y));
  BasicReg8 saida0 (.Q(saida0_q), .D(cpu8bit1k_1_out), .E(decoder4e_1__0), .CLK(div50m1khz_1_y));
  BasicReg8 saida1 (.Q(saida1_q), .D(cpu8bit1k_1_out), .E(decoder4e_1__1), .CLK(div50m1khz_1_y));
  assign {not_1_out, L3, L2, L1, L0} = ~saida2_q;  // Not not_1, 8 bits wide
  // Probe on saida2_q
  // Probe on saida0_q
  // Probe on saida1_q
  Counter #(.Bits(2)) counter_1 (.en(1'b1), .C(div50m1khz_1_y), .clr(1'b0), .out(counter_1_out));  // open: ovf
  Multiplexer #(.Selector_Bits(2), .Bits(4)) multiplexer_1 (
    .sel(counter_1_out), .in_0(saida0_q[3:0]), .in_1(saida0_q[7:4]), .in_2(saida1_q[3:0]),
    .in_3(saida1_q[7:4]), .out(multiplexer_1_out));
  Driver7Seg driver7seg_1 (
    .D0(multiplexer_1_out[0]), .D1(multiplexer_1_out[1]), .D2(multiplexer_1_out[2]),
    .D3(multiplexer_1_out[3]), .Inv(1'b1), .a(a), .b(b), .c(c), .d(d), .e(e), .f(f), .g(g));
  Decoder #(.Selector_Bits(2)) decoder_1 (
    .sel(counter_1_out), .out_0(decoder_1_out_0), .out_1(decoder_1_out_1), .out_2(decoder_1_out_2),
    .out_3(decoder_1_out_3));
  not not_2 (dig0, decoder_1_out_0);
  not not_3 (dig1, decoder_1_out_1);
  not not_4 (dig2, decoder_1_out_2);
  not not_5 (dig3, decoder_1_out_3);

  assign dp = 1'b1;

  // Notes on the sheet:
  //   Clock: Hz: 1000
  //   PROM loads out.hex
endmodule
